# Fritzing sketch Sketch (saved by Fritzing 1.0.2b)

parts:
  Raspberry_Pi_1 = Raspberry Pi 3 [part_number=RPI-3-V1.2]
  LED1 = LED - 5mm [color="Infrared (940nm)" current=0.030A package="5 mm [THT]"]
  R1 = Resistor [tolerance=±5% power=0.25W resistance=220 package=THT]
  R2 = Resistor [tolerance=±5% power=0.25W resistance=4.7k package=THT]
  D1 = LTE-302 [package=lte-302]

nets:
  N1: Raspberry_Pi_1.GND, LED1.cathode, D1.C
  N2: Raspberry_Pi_1.GPIO24, R1.Pin_1
  N3: Raspberry_Pi_1.GPIO23, R2.Pin_0, D1.A
  N4: Raspberry_Pi_1.5V, R2.Pin_1
  N5: LED1.anode, R1.Pin_0

notes:
  <-- Point your remote here
  Point the LED to your TV, RGB Light, etc
